# Fritzing sketch angryOwlSche (saved by Fritzing 0.9.3b)
breadboards: 3

parts:
  MCU1 = Raspberry Pi Zero
  Left_Wing = DC Motor
  Left_Wheel = DC Motor
  U1 = MBED_NXP_LPC1768 [package=dil40_0.9]
  Part1 = Motor Driver 1A Dual TB6612FNG
  VCC1 = 4 x AAA Battery Mount
  Left_Wing1 = DC Motor
  Left_Wheel1 = DC Motor
  Part2 = Motor Driver 1A Dual TB6612FNG
  microSD_Transflash1 = SparkFun - microSD Transflash
  SPKR1 = Loudspeaker
  Lhi1 = LHi958 [package=to-39]
  U2 = Mono 2.6W Class D Amplifier [package=8-tdfn-ep]
  LED1 = LED - 5mm [color="Red (633nm)" package="5 mm [THT]"]
  LED2 = LED - 5mm [color="Red (633nm)" package="5 mm [THT]"]
  R1 = Resistor [tolerance=±5% resistance=220 package=THT]
  R2 = Resistor [tolerance=±5% resistance=220 package=THT]
  Lhi2 = LHi958 [package=to-39]
  Lhi3 = LHi958 [package=to-39]

nets:
  N1: MCU1.pin_2, MCU1.pin_4, Lhi1.D, Lhi2.D, Lhi3.D
  GND: MCU1.pin_9, Lhi1.GND, Lhi2.GND, Lhi3.GND
  N2: MCU1.pin_11, Lhi2.S
  N3: MCU1.pin_13, Lhi1.S
  N4: MCU1.pin_15, Lhi3.S
  N5: Left_Wing.pin_1, Part1.B01
  N6: Left_Wing.pin_2, Part1.B02
  N7: Left_Wheel.pin_1, Part2.A02
  N8: Left_Wheel.pin_2, Part2.A01
  GND_2: U1.P$1, Part1.GND, VCC1.-, Part2.GND, microSD_Transflash1.GND, U2.GND, LED1.cathode, LED2.cathode
  N9: U1.P$5, microSD_Transflash1.DI
  N10: U1.P$6, microSD_Transflash1.DO
  N11: U1.P$7, microSD_Transflash1.SCK
  N12: U1.P$8, microSD_Transflash1.CS
  N13: U1.P$9, Part1.AIN2
  N14: U1.P$10, Part1.AIN1
  N15: U1.P$11, Part1.BIN2
  N16: U1.P$12, Part1.BIN1
  N17: U1.P$13, Part2.AIN1
  N18: U1.P$14, Part2.AIN2
  N19: U1.P$15, Part2.BIN2
  N20: U1.P$16, Part2.BIN1
  N21: U1.P$18, U2.IN+
  N22: U1.P$21, Part1.PWMB
  N23: U1.P$22, Part1.PWMA
  N24: U1.P$23, R2.Pin_1
  N25: U1.P$24, Part2.PWMA
  N26: U1.P$25, Part2.PWMB
  N27: U1.P$26, R1.Pin_1
  VCC: U1.P$40, Part1.VCC, Part1.STBY, Part2.VCC, Part2.STBY, microSD_Transflash1.VCC, U2.VDD
  N28: Part1.A02, Left_Wing1.pin_1
  N29: Part1.A01, Left_Wing1.pin_2
  N30: Part1.VM, VCC1.+, Part2.VM
  N31: Left_Wheel1.pin_1, Part2.B01
  N32: Left_Wheel1.pin_2, Part2.B02
  N33: SPKR1.pin1, U2.OUT-
  N34: SPKR1.pin2, U2.OUT+
